# Fritzing sketch adalogger_k30_powerBoost (saved by Fritzing 0.9.4)

parts:
  Part1 = Adafruit Feather M0 Adalogger [part_number="Adafruit #2796"]
  Part2 = PowerBoost 500 Charger
  K1 = CO2 sensor [package=PCB]
  U1 = LIPO-1000mAh [package=lipo-1000]  # not connected

nets:
  GND: Part1.GND, Part2.GND, K1.G0
  N1: Part1.D1, K1.RxD_UART
  N2: Part1.D0, K1.TxD_UART
  N3: Part1.VBAT, Part2.VBAT_OUT
  N4: Part2.5.0V, K1.G+

custom parts:
  Adafruit Feather M0 Adalogger: This is the Adafruit Feather M0 Adalogger - our take on an 'all-in-one' Cortex M0 datalogger (or data-reader) with built in USB and battery charging. Its an Adafruit Feather M0 with a microSD holder ready to rock! We have other boards in the Feather family, check'em out here At the Feather M0's heart is an ATSAMD21G18 ARM Cortex M0 processor, clocked at 48 MHz and at 3.3V logic, the same one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
  CO2 sensor: A CO2 sensor from CO2Meter - K30. Datasheet http://co2meters.com/Documentation/Datasheets/DS30-01%20-%20K30.pdf Could not make fine PCB and principal. You should make yours if needed.
